// Logisim project SAP-1.circ as structural Verilog: 6 circuits, main circuit main
module main (
  input  Ep,
  input  Cp,
  input  nCLR,
  input  nCLK,
  input  BUS_3,
  input  BUS_2,
  input  BUS_1,
  input  BUS_0,
  input  nLM,
  input  CLK,
  input  RUN_PROG,
  input  A3,
  input  A2,
  input  A1,
  input  A0,
  output B0,
  output B1,
  output B2,
  output B3,
  output out_20,
  output out_21,
  output out_22,
  output out_23
);

  wire n74ls107_1_q1, n74ls107_1_q2, n74ls107_2_q1, n74ls107_2_q2, n74ls173_1__1q, n74ls173_1__2q,
       n74ls173_1__3q, n74ls173_1__4q;

  _74LS107 u_74ls107_1 (
    .J1(Cp), .CLK1(nCLK), .K1(Cp), .nCLR1(nCLR), .J2(Cp), .CLK2(n74ls107_1_q1), .K2(Cp), .nCLR2(nCLR),
    .Vcc(1'b1), .Gnd(1'b0), .Q1(n74ls107_1_q1), .Q2(n74ls107_1_q2));  // open: Q_n1, Q_n1_2
  _74LS107 u_74ls107_2 (
    .J1(Cp), .CLK1(n74ls107_1_q2), .K1(Cp), .nCLR1(nCLR), .J2(Cp), .CLK2(n74ls107_2_q1), .K2(Cp),
    .nCLR2(nCLR), .Vcc(1'b1), .Gnd(1'b0), .Q1(n74ls107_2_q1), .Q2(n74ls107_2_q2));  // open: Q_n1, Q_n1_2
  _74LS126 u_74ls126_1 (
    .GND(1'b0), .Vcc(1'b1), ._1A(n74ls107_1_q1), ._1G(Ep), ._2A(n74ls107_1_q2), ._2G(Ep),
    ._3A(n74ls107_2_q1), ._3G(Ep), ._4A(n74ls107_2_q2), ._4G(Ep), ._1Y(B0), ._2Y(B1), ._3Y(B2), ._4Y(B3));
  _74LS173 u_74ls173_1 (
    .Vcc(1'b1), .M(1'b0), .N(1'b0), ._1Q(n74ls173_1__1q), ._1D(BUS_3), .nG1(nLM), .nG2(nLM),
    ._2Q(n74ls173_1__2q), ._2D(BUS_2), ._3Q(n74ls173_1__3q), ._3D(BUS_1), ._4D(BUS_0), .CLK(CLK), .CLR(1'b0),
    .GND(1'b0), ._4Q(n74ls173_1__4q));
  // DIP_74157 dip_74157_1: pin names not known; wires that end beside it: RUN_PROG, A0, n74ls173_1__4q, out_23, A1, n74ls173_1__3q, out_22, 1'b0, A3, n74ls173_1__1q, out_20, A2, n74ls173_1__2q, out_21
endmodule

module program_counter (
  input  Ep,
  input  Cp,
  input  nCLR,
  input  nCLK,
  output B0,
  output B1,
  output B2,
  output B3
);

  wire n74ls107_1_q1, n74ls107_1_q2, n74ls107_2_q1, n74ls107_2_q2;

  _74LS107 u_74ls107_1 (
    .J1(Cp), .CLK1(nCLK), .K1(Cp), .nCLR1(nCLR), .J2(Cp), .CLK2(n74ls107_1_q1), .K2(Cp), .nCLR2(nCLR),
    .Vcc(1'b1), .Gnd(1'b0), .Q1(n74ls107_1_q1), .Q2(n74ls107_1_q2));  // open: Q_n1, Q_n1_2
  _74LS107 u_74ls107_2 (
    .J1(Cp), .CLK1(n74ls107_1_q2), .K1(Cp), .nCLR1(nCLR), .J2(Cp), .CLK2(n74ls107_2_q1), .K2(Cp),
    .nCLR2(nCLR), .Vcc(1'b1), .Gnd(1'b0), .Q1(n74ls107_2_q1), .Q2(n74ls107_2_q2));  // open: Q_n1, Q_n1_2
  _74LS126 u_74ls126_1 (
    .GND(1'b0), .Vcc(1'b1), ._1A(n74ls107_1_q1), ._1G(Ep), ._2A(n74ls107_1_q2), ._2G(Ep),
    ._3A(n74ls107_2_q1), ._3G(Ep), ._4A(n74ls107_2_q2), ._4G(Ep), ._1Y(B0), ._2Y(B1), ._3Y(B2), ._4Y(B3));
endmodule

module _74LS107 (
  input  J1,
  input  CLK1,
  input  K1,
  input  nCLR1,
  input  J2,
  input  CLK2,
  input  K2,
  input  nCLR2,
  input  Vcc,
  input  Gnd,
  output Q1,
  output Q_n1,
  output Q2,
  output Q_n1_2
);

  wire not_1_out, not_2_out, not_3_out, not_4_out;

  not not_1 (not_1_out, CLK1);
  not not_2 (not_2_out, nCLR1);
  not not_3 (not_3_out, CLK2);
  not not_4 (not_4_out, nCLR2);
  J_K_Flip_Flop j_k_ff_1 (.J(J1), .clk(not_1_out), .K(K1), .Q(Q1), .Qn(Q_n1), .reset(not_2_out));  // open: preset, en
  J_K_Flip_Flop j_k_ff_2 (.J(J2), .clk(not_3_out), .K(K2), .Q(Q2), .Qn(Q_n1_2), .reset(not_4_out));  // open: preset, en
endmodule

module _74LS126 (
  input  GND,
  input  Vcc,
  input  _1A,
  input  _1G,
  input  _2A,
  input  _2G,
  input  _3A,
  input  _3G,
  input  _4A,
  input  _4G,
  output _1Y,
  output _2Y,
  output _3Y,
  output _4Y
);

  assign _1Y = _1G ? _1A : 1'bz;  // Controlled_Buffer controlled_buffer_1
  assign _2Y = _2G ? _2A : 1'bz;  // Controlled_Buffer controlled_buffer_2
  assign _3Y = _3G ? _3A : 1'bz;  // Controlled_Buffer controlled_buffer_3
  assign _4Y = _4G ? _4A : 1'bz;  // Controlled_Buffer controlled_buffer_4
endmodule

module MAR (
  input  BUS_3,
  input  BUS_2,
  input  BUS_1,
  input  BUS_0,
  input  nLM,
  input  CLK,
  input  RUN_PROG,
  input  A3,
  input  A2,
  input  A1,
  input  A0,
  output out_12,
  output out_13,
  output out_14,
  output out_15
);

  wire n74ls173_1__1q, n74ls173_1__2q, n74ls173_1__3q, n74ls173_1__4q;

  _74LS173 u_74ls173_1 (
    .Vcc(1'b1), .M(1'b0), .N(1'b0), ._1Q(n74ls173_1__1q), ._1D(BUS_3), .nG1(nLM), .nG2(nLM),
    ._2Q(n74ls173_1__2q), ._2D(BUS_2), ._3Q(n74ls173_1__3q), ._3D(BUS_1), ._4D(BUS_0), .CLK(CLK), .CLR(1'b0),
    .GND(1'b0), ._4Q(n74ls173_1__4q));
  // DIP_74157 dip_74157_1: pin names not known; wires that end beside it: RUN_PROG, A0, n74ls173_1__4q, out_15, A1, n74ls173_1__3q, out_14, 1'b0, A3, n74ls173_1__1q, out_12, A2, n74ls173_1__2q, out_13
endmodule

module _74LS173 (
  input  Vcc,
  input  M,
  input  N,
  input  _1D,
  input  nG1,
  input  nG2,
  input  _2D,
  input  _3D,
  input  _4D,
  input  CLK,
  input  CLR,
  input  GND,
  output _1Q,
  output _2Q,
  output _3Q,
  output _4Q
);

  wire and_1_out, and_2_out, and_3_out, and_4_out, and_5_out, and_6_out, and_7_out, and_8_out, and_9_out,
       and_10_out, not_1_out, or_1_out, or_2_out, or_3_out, or_4_out, register_1_q, register_2_q,
       register_3_q, register_4_q;

  and and_1 (and_1_out, ~M, ~N);  // AND_Gate
  not not_1 (not_1_out, and_2_out);
  and and_2 (and_2_out, ~nG1, ~nG2);  // AND_Gate
  and and_3 (and_3_out, register_1_q, not_1_out);
  and and_4 (and_4_out, _1D, and_2_out);
  and and_5 (and_5_out, register_2_q, not_1_out);
  and and_6 (and_6_out, _2D, and_2_out);
  and and_7 (and_7_out, register_3_q, not_1_out);
  and and_8 (and_8_out, _3D, and_2_out);
  and and_9 (and_9_out, register_4_q, not_1_out);
  and and_10 (and_10_out, _4D, and_2_out);
  Register #(.width(1)) register_1 (.D(or_1_out), .en(Vcc), .Q(register_1_q), .clk(CLK), .clr(CLR));
  or or_1 (or_1_out, and_3_out, and_4_out);
  or or_2 (or_2_out, and_5_out, and_6_out);
  Register #(.width(1)) register_2 (.D(or_2_out), .en(Vcc), .Q(register_2_q), .clk(CLK));  // open: clr
  Register #(.width(1)) register_3 (.D(or_3_out), .en(Vcc), .Q(register_3_q), .clk(CLK), .clr(CLR));
  or or_3 (or_3_out, and_7_out, and_8_out);
  Register #(.width(1)) register_4 (.D(or_4_out), .en(Vcc), .Q(register_4_q), .clk(CLK), .clr(CLR));
  or or_4 (or_4_out, and_9_out, and_10_out);
  assign _1Q = and_1_out ? register_1_q : 1'bz;  // Controlled_Buffer controlled_buffer_1
  assign _2Q = and_1_out ? register_2_q : 1'bz;  // Controlled_Buffer controlled_buffer_2
  assign _3Q = and_1_out ? register_3_q : 1'bz;  // Controlled_Buffer controlled_buffer_3
  assign _4Q = and_1_out ? register_4_q : 1'bz;  // Controlled_Buffer controlled_buffer_4
endmodule
